# Fritzing sketch circuit (saved by Fritzing 0.7.10b)
breadboards: 1

parts:
  U1 = mystery part, 20 pins [chip_label=?]
  R4 = Resistor [tolerance=±5% resistance=10k package=THT]
  R5 = Resistor [tolerance=±5% resistance=10k package=THT]
  R6 = Resistor [tolerance=±5% resistance=10k package=THT]
  R7 = Resistor [tolerance=±5% resistance=10k package=THT]
  R8 = Resistor [tolerance=±5% resistance=10k package=THT]
  R9 = Resistor [tolerance=±5% resistance=10k package=THT]
  S1 = Pushbutton [package=THT]
  R12 = Rotary Potentiometer (Small) [maximum_resistance=100kΩ]
  S2 = Toggle Switch [package=THT]
  R13 = Resistor [tolerance=±5% resistance=220 package=THT]
  R11 = Resistor [tolerance=±5% resistance=220 package=THT]
  R10 = Resistor [tolerance=±5% resistance=10k package=THT]
  R3 = Resistor [tolerance=±5% resistance=10k package=THT]
  R2 = Resistor [tolerance=±5% resistance=10k package=THT]
  R1 = Resistor [tolerance=±5% resistance=10k package=THT]
  Arduino1 = Arduino

nets (from the pcb view):
  N1: U1.pin1, R10.Pin_0
  N2: U1.pin2, R9.Pin_0
  N3: U1.pin3, R8.Pin_0
  N4: U1.pin4, R7.Pin_0
  N5: U1.pin5, R6.Pin_0
  N6: U1.pin6, R5.Pin_0
  N7: U1.pin7, R4.Pin_0
  N8: U1.pin8, R3.Pin_0
  N9: U1.pin9, R2.Pin_0
  N10: U1.pin10, R1.Pin_0
  N11: U1.pin11, U1.pin12, U1.pin13, U1.pin14, U1.pin15, U1.pin16, U1.pin17, U1.pin18, U1.pin19, U1.pin20, R12.leg2, R13.Pin_1, R11.Pin_0, Arduino1.GND
  N12: R4.Pin_1, Arduino1.D8
  N13: R5.Pin_1, Arduino1.D7
  N14: R6.Pin_1, Arduino1.D6
  N15: R7.Pin_1, Arduino1.D5
  N16: R8.Pin_1, Arduino1.D4
  N17: R9.Pin_1, Arduino1.D3
  N18: S1.leg0, R12.leg1, S2.L1, Arduino1.+5V
  N19: S1.leg1, R11.Pin_1, Arduino1.A0
  N20: R12.wiper, Arduino1.A1
  N21: S2.COM, R13.Pin_0, Arduino1.A2
  N22: R10.Pin_1, Arduino1.D2
  N23: R3.Pin_1, Arduino1.D9
  N24: R2.Pin_1, Arduino1.D10
  N25: R1.Pin_1, Arduino1.D11
